# Fritzing sketch fritzing_layout (saved by Fritzing 0.9.3b)
perfboards: 1

parts:
  WTV020-SD = WTV020SD [package=ssop_20]
  HC-SR501 = PIR sensor
  YL-69 = YL-83 Rain Sensor - Control Board
  Part1 = FC-28 Soil Hygrometer Module - Probe
  Speaker = SPEAKER [package=pcb_mount_speaker]
  U1 = LIPO-2000mAh [package=lipo-2000]
  MCP73831T = USB LiPoly Charger
  Arduino_Nano_/_Pro_Clone = Arduino Nano (Rev3.0)

nets:
  N1: WTV020-SD.P03, Arduino_Nano_/_Pro_Clone.A0
  N2: WTV020-SD.P06, Speaker.-
  N3: WTV020-SD.P07, Speaker.+
  N4: WTV020-SD.SPK_P, Arduino_Nano_/_Pro_Clone.A1
  GND: WTV020-SD.SPK_N, HC-SR501.GND, YL-69.GND, U1.-, MCP73831T.GND, Arduino_Nano_/_Pro_Clone.GND
  N5: WTV020-SD.PAD_EQO, Arduino_Nano_/_Pro_Clone.A2
  VDD: WTV020-SD.P00, HC-SR501.VDD, YL-69.VCC, U1.+, MCP73831T.VBAT, Arduino_Nano_/_Pro_Clone.5V
  N6: HC-SR501.SIG, Arduino_Nano_/_Pro_Clone.D10
  N7: YL-69.AO, Arduino_Nano_/_Pro_Clone.A3
  N8: YL-69.POS, Part1.POS
  N9: YL-69.NEG, Part1.NEG
  N10: MCP73831T.pin_12, Arduino_Nano_/_Pro_Clone.A6

custom parts:
  YL-83 Rain Sensor - Control Board: The YL-83 is a rain sensor that has more resistance when dry and less resistance when wet. The module runs at 5V.
  FC-28 Soil Hygrometer Module - Probe: The FC-28 is a soil hygrometer module that uses the Texas Instruments LM393 comparator chip to provide an analog measurement of soil humidity.
  USB LiPoly Charger: Description: If you need to charge LiPo batteries, this simple charger will do just that, and do it fast! The USB LiPo Charger is a basic charging circuit that allows you to charge 3.7V LiPo cells at a rate of 500mA or 100mA per hour. It is designed to charge single-cell Li-Ion or Li-Polymer batteries. Check the datasheet below to see if it will work with your battery. The board incorporates a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
